# Fritzing sketch PCB (saved by Fritzing 0.9.3b)
perfboards: 1

parts:
  Componente2 = Arduino Nano (Rev3.0)
  Componente3 = Motor Driver 1A Dual TB6612FNG
  S1 = SPST Switch [package=switch-spdt]

nets:
  N1: Componente2.VIN, S1.O
  5V: Componente2.5V, Componente3.VCC
